# Fritzing sketch ElectronicDecider (saved by Fritzing 0.9.1b)
breadboards: 1

parts:
  Composant1 = Arduino Uno (Rev3)
  LED1 = LED - 3mm [color="Green (555nm)" package="3 mm [THT]"]
  LED2 = LED - 3mm [color="Red (633nm)" package="3 mm [THT]"]
  S2 = Pushbutton [package="[SMD]"]
  R2 = Resistor [tolerance=±5% resistance=560 package="0805 [SMD]"]
  R3 = Resistor [tolerance=±5% resistance=560 package="0805 [SMD]"]
  R4 = Resistor [tolerance=±5% resistance=10k package="0805 [SMD]"]

nets:
  N1: Composant1.D2, S2.Pin_1, S2.Pin_2, R4.Pin_0
  N2: Composant1.D3_PWM, R3.Pin_1
  N3: Composant1.D4, R2.Pin_1
  N4: Composant1.5V, S2.Pin_3, S2.Pin_4
  N5: Composant1.GND, LED1.cathode, LED2.cathode, R4.Pin_1
  N6: LED1.anode, R3.Pin_0
  N7: LED2.anode, R2.Pin_0
