# Fritzing sketch RemoteDSLRTrigger_v0 - With button and NPN transistor - Copy (saved by Fritzing 0.9.1b)
breadboards: 1

parts:
  S2 = Pushbutton [package="[THT]"]
  LED1 = smd LED [color="Green (555nm)" package="1206 [SMD]"]
  LED2 = smd LED [color="Infrared (940nm)" package="1206 [SMD]"]
  Composant1 = Arduino Uno (Rev3)
  R1 = Resistor [tolerance=±5% resistance=560 package="0603 [SMD]"]
  R2 = Resistor [tolerance=±5% resistance=222 package="0603 [SMD]"]
  R3 = Resistor [tolerance=±5% resistance=10k package="0603 [SMD]"]
  Q1 = NPN-Transistor [package="SOT-23 [SMD]"]
  R4 = Resistor [tolerance=±5% resistance=222 package="0603 [SMD]"]

nets:
  N1: S2.Pin_1, S2.Pin_2, Composant1.D2, R3.Pin_0
  N2: S2.Pin_3, S2.Pin_4, LED2.anode, Composant1.5V
  N3: LED1.cathode, Composant1.GND, R3.Pin_1, Q1.2
  N4: LED1.anode, R1.Pin_0
  N5: LED2.cathode, R2.Pin_1
  N6: Composant1.D9_PWM, R4.Pin_0
  N7: Composant1.D13/SCK, R1.Pin_1
  N8: R2.Pin_0, Q1.1
  N9: Q1.0, R4.Pin_1
