# Fritzing sketch RemoteDSLRTrigger_v1 (saved by Fritzing 0.9.1b)
breadboards: 1

parts:
  LED1 = smd LED [color="Green (555nm)" package="1206 [SMD]"]
  LED2 = smd LED [color="Infrared (940nm)" package="1206 [SMD]"]
  Composant1 = Arduino Uno (Rev3)
  R1 = Resistor [tolerance=±5% resistance=560 package="0603 [SMD]"]
  R2 = Resistor [tolerance=±5% resistance=27 package="0603 [SMD]"]

nets:
  N1: LED1.cathode, Composant1.GND, R2.Pin_0
  N2: LED1.anode, R1.Pin_0
  N3: LED2.cathode, R2.Pin_1
  N4: LED2.anode, Composant1.D9_PWM
  N5: Composant1.D13/SCK, R1.Pin_1
